# Fritzing sketch ender2pro-wiring (saved by Fritzing 0.9.10b)

parts:
  Raspberry_Pi_1 = Raspberry Pi 3 [part_number=RPI-3-V1.2]
  M1 = RioRand LM2596
  M2 = RioRand LM2596
  Printer_Mainboard_Fan_(40mm) = Fan - 4 wire [package=THT]
  Hot-End_Light = 12 NeoPixel Ring [part_number=1643]
  Accel_Sensor = Triple Axis Accelerometer Breakout - ADXL345

nets:
  3V3: Raspberry_Pi_1.3v3, Hot-End_Light.VDD
  N1: Raspberry_Pi_1.GIPO10, Accel_Sensor.SDA
  N2: Raspberry_Pi_1.GIPO9, Accel_Sensor.SDO
  N3: Raspberry_Pi_1.GIPO11, Accel_Sensor.SCL
  N4: Raspberry_Pi_1.GIPO16, Hot-End_Light.IN
  GND: Raspberry_Pi_1.GND, M2.Pin_4, Hot-End_Light.GND, Accel_Sensor.GND
  N5: Raspberry_Pi_1.GIPO8, Accel_Sensor.CS
  5V: Raspberry_Pi_1.5V, M2.Pin_3, Accel_Sensor.VCC
  N6: M1.Pin_3, Printer_Mainboard_Fan_(40mm).Power
  N7: M1.Pin_4, Printer_Mainboard_Fan_(40mm).GND

custom parts:
  Fan - 4 wire: Fan, 4 wire with tach.
  12 NeoPixel Ring: 12 ultra bright smart LED NeoPixels are arranged in a circle with 1.5" (37mm) outer diameter. The rings are 'chainable' - connect the output pin of one to the input pin of another. Use only one microcontroller pin to control as many as you can chain together! Each LED is addressable as the driver chip is inside the LED. Each one has ~18mA constant current drive so the color will be very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
